// Logisim project mips_alunos.circ as structural Verilog: 10 circuits, main circuit ULA 32 Bits
module CPU_MIPS (
);

  wire and_1_out, button_1_out, clock_1_out, UC_alusrc, UC_branch, UC_memread, UC_memtoreg, UC_memwrite,
       UC_regdst, UC_regwrite, ULA_zero;
  wire [1:0] UC_aluop;
  wire [3:0] UC_ULA_alucontrol;
  wire [4:0] Divisor_rd, Divisor_rs, Divisor_rt, multiplexer_1_out;
  wire [5:0] Divisor_funct, Divisor_op;
  wire [15:0] Divisor_imediato;
  wire [31:0] adder_1_out, adder_2_out, bit_extender_1_out, BR_a, BR_b, Mem_Data_dataout, Mem_Inst_out_2,
       multiplexer_2_out, multiplexer_3_out, multiplexer_4_out, PC_q, ULA_resultado;

  Clock clock_1 (.out(clock_1_out));
  Button button_1 (.out(button_1_out));
  Register #(.width(32), .trigger("falling")) PC (
    .D(multiplexer_2_out), .Q(PC_q), .clk(clock_1_out), .clr(button_1_out));  // open: en
  UC UC (
    .OP(Divisor_op), .RegDst(UC_regdst), .ALUSrc(UC_alusrc), .MemtoReg(UC_memtoreg), .RegWrite(UC_regwrite),
    .MemRead(UC_memread), .MemWrite(UC_memwrite), .Branch(UC_branch), .ALUOP(UC_aluop));
  Adder #(.width(32)) adder_1 (.a(PC_q), .b(bit_extender_1_out), .out(adder_1_out));  // open: cin, cout
  Adder #(.width(32)) adder_2 (.a(PC_q), .b(32'h1), .out(adder_2_out));  // open: cin, cout
  Divisor Divisor (
    .Instrucao(Mem_Inst_out_2), .OP(Divisor_op), .RS(Divisor_rs), .RT(Divisor_rt), .RD(Divisor_rd),
    .FUNCT(Divisor_funct), .Imediato(Divisor_imediato));  // open: SHAMT
  Mem_Inst Mem_Inst (.Endereco(PC_q), .out_2(Mem_Inst_out_2));
  Multiplexer #(.width(5), .enable("false")) multiplexer_1 (
    .in0(Divisor_rt), .in1(Divisor_rd), .out(multiplexer_1_out), .sel(UC_regdst));
  Multiplexer #(.width(32), .enable("false")) multiplexer_2 (
    .in0(adder_1_out), .in1(adder_2_out), .out(multiplexer_2_out), .sel(and_1_out));
  Banco_de_Registradores_32 BR (
    .RS(Divisor_rs), .RT(Divisor_rt), .RD(multiplexer_1_out), .WriteReg(UC_regwrite),
    .DataIn(multiplexer_4_out), .A(BR_a), .B(BR_b));
  and and_1 (and_1_out, UC_branch, ULA_zero);
  Multiplexer #(.width(32), .enable("false")) multiplexer_3 (
    .in0(BR_b), .in1(bit_extender_1_out), .out(multiplexer_3_out), .sel(UC_alusrc));
  assign bit_extender_1_out = {{16{Divisor_imediato[15]}}, Divisor_imediato};  // Bit_Extender bit_extender_1
  UC_ULA UC_ULA (.Funct(Divisor_funct), .ALUOP(UC_aluop), .Alucontrol(UC_ULA_alucontrol));
  ULA_32_Bits ULA (
    .A(BR_a), .B(multiplexer_3_out), .Control(UC_ULA_alucontrol), .Resultado(ULA_resultado), .Zero(ULA_zero));
  Mem_Data Mem_Data (
    .Endereco(ULA_resultado), .Read(UC_memread), .Write(UC_memwrite), .DataOut(Mem_Data_dataout));  // open: DataIn
  Multiplexer #(.width(32), .enable("false")) multiplexer_4 (
    .in0(ULA_resultado), .in1(Mem_Data_dataout), .out(multiplexer_4_out), .sel(UC_memtoreg));
endmodule

module Banco_de_Registradores_32 (
  input  WriteReg,
  input  [4:0] RS,
  input  [4:0] RT,
  input  [4:0] RD,
  input  [31:0] DataIn,
  output [31:0] A,
  output [31:0] B
);

  wire decoder_1_out1, decoder_1_out2, decoder_1_out3, decoder_1_out4, decoder_1_out5, decoder_1_out6,
       decoder_1_out7, decoder_1_out8, decoder_1_out9, decoder_1_out10, decoder_1_out11, decoder_1_out12,
       decoder_1_out13, decoder_1_out14, decoder_1_out15, decoder_1_out16, decoder_1_out17, decoder_1_out18,
       decoder_1_out19, decoder_1_out20, decoder_1_out21, decoder_1_out22, decoder_1_out23, decoder_1_out24,
       decoder_1_out25, decoder_1_out26, decoder_1_out27, decoder_1_out28, decoder_1_out29, decoder_1_out30,
       decoder_1_out31;
  wire [31:0] register_1_q, register_2_q, register_3_q, register_4_q, register_5_q, register_6_q,
       register_7_q, register_8_q, register_9_q, register_10_q, register_11_q, register_12_q, register_13_q,
       register_14_q, register_15_q, register_16_q, register_17_q, register_18_q, register_19_q,
       register_20_q, register_21_q, register_22_q, register_23_q, register_24_q, register_25_q,
       register_26_q, register_27_q, register_28_q, register_29_q, register_30_q, register_31_q,
       register_32_q;

  Decoder #(.select(5)) decoder_1 (
    .out1(decoder_1_out1), .out2(decoder_1_out2), .out3(decoder_1_out3), .out4(decoder_1_out4),
    .out5(decoder_1_out5), .out6(decoder_1_out6), .out7(decoder_1_out7), .out8(decoder_1_out8),
    .out9(decoder_1_out9), .out10(decoder_1_out10), .out11(decoder_1_out11), .out12(decoder_1_out12),
    .out13(decoder_1_out13), .out14(decoder_1_out14), .out15(decoder_1_out15), .out16(decoder_1_out16),
    .out17(decoder_1_out17), .out18(decoder_1_out18), .out19(decoder_1_out19), .out20(decoder_1_out20),
    .out21(decoder_1_out21), .out22(decoder_1_out22), .out23(decoder_1_out23), .out24(decoder_1_out24),
    .out25(decoder_1_out25), .out26(decoder_1_out26), .out27(decoder_1_out27), .out28(decoder_1_out28),
    .out29(decoder_1_out29), .out30(decoder_1_out30), .out31(decoder_1_out31), .sel(RD), .en(WriteReg));  // open: out0
  Register #(.width(32)) register_1 (.D(DataIn), .Q(register_1_q));  // open: en, clk, clr
  Register #(.width(32)) register_2 (
    .D(DataIn), .en(decoder_1_out1), .Q(register_2_q), .clk(decoder_1_out1));  // open: clr
  Register #(.width(32)) register_3 (
    .D(DataIn), .en(decoder_1_out2), .Q(register_3_q), .clk(decoder_1_out2));  // open: clr
  Register #(.width(32)) register_4 (
    .D(DataIn), .en(decoder_1_out3), .Q(register_4_q), .clk(decoder_1_out3));  // open: clr
  Register #(.width(32)) register_5 (
    .D(DataIn), .en(decoder_1_out4), .Q(register_5_q), .clk(decoder_1_out4));  // open: clr
  Register #(.width(32)) register_6 (
    .D(DataIn), .en(decoder_1_out5), .Q(register_6_q), .clk(decoder_1_out5));  // open: clr
  Register #(.width(32)) register_7 (
    .D(DataIn), .en(decoder_1_out6), .Q(register_7_q), .clk(decoder_1_out6));  // open: clr
  Register #(.width(32)) register_8 (
    .D(DataIn), .en(decoder_1_out7), .Q(register_8_q), .clk(decoder_1_out7));  // open: clr
  Register #(.width(32)) register_9 (
    .D(DataIn), .en(decoder_1_out8), .Q(register_9_q), .clk(decoder_1_out8));  // open: clr
  Register #(.width(32)) register_10 (
    .D(DataIn), .en(decoder_1_out9), .Q(register_10_q), .clk(decoder_1_out9));  // open: clr
  Register #(.width(32)) register_11 (
    .D(DataIn), .en(decoder_1_out10), .Q(register_11_q), .clk(decoder_1_out10));  // open: clr
  Register #(.width(32)) register_12 (
    .D(DataIn), .en(decoder_1_out11), .Q(register_12_q), .clk(decoder_1_out11));  // open: clr
  Register #(.width(32)) register_13 (
    .D(DataIn), .en(decoder_1_out12), .Q(register_13_q), .clk(decoder_1_out12));  // open: clr
  Register #(.width(32)) register_14 (
    .D(DataIn), .en(decoder_1_out13), .Q(register_14_q), .clk(decoder_1_out13));  // open: clr
  Register #(.width(32)) register_15 (
    .D(DataIn), .en(decoder_1_out14), .Q(register_15_q), .clk(decoder_1_out14));  // open: clr
  Register #(.width(32)) register_16 (
    .D(DataIn), .en(decoder_1_out15), .Q(register_16_q), .clk(decoder_1_out15));  // open: clr
  Register #(.width(32)) register_17 (
    .D(DataIn), .en(decoder_1_out16), .Q(register_17_q), .clk(decoder_1_out16));  // open: clr
  Register #(.width(32)) register_18 (
    .D(DataIn), .en(decoder_1_out17), .Q(register_18_q), .clk(decoder_1_out17));  // open: clr
  Register #(.width(32)) register_19 (
    .D(DataIn), .en(decoder_1_out18), .Q(register_19_q), .clk(decoder_1_out18));  // open: clr
  Register #(.width(32)) register_20 (
    .D(DataIn), .en(decoder_1_out19), .Q(register_20_q), .clk(decoder_1_out19));  // open: clr
  Register #(.width(32)) register_21 (
    .D(DataIn), .en(decoder_1_out20), .Q(register_21_q), .clk(decoder_1_out20));  // open: clr
  Register #(.width(32)) register_22 (
    .D(DataIn), .en(decoder_1_out21), .Q(register_22_q), .clk(decoder_1_out21));  // open: clr
  Register #(.width(32)) register_23 (
    .D(DataIn), .en(decoder_1_out22), .Q(register_23_q), .clk(decoder_1_out22));  // open: clr
  Register #(.width(32)) register_24 (
    .D(DataIn), .en(decoder_1_out23), .Q(register_24_q), .clk(decoder_1_out23));  // open: clr
  Register #(.width(32)) register_25 (
    .D(DataIn), .en(decoder_1_out24), .Q(register_25_q), .clk(decoder_1_out24));  // open: clr
  Register #(.width(32)) register_26 (
    .D(DataIn), .en(decoder_1_out25), .Q(register_26_q), .clk(decoder_1_out25));  // open: clr
  Register #(.width(32)) register_27 (
    .D(DataIn), .en(decoder_1_out26), .Q(register_27_q), .clk(decoder_1_out26));  // open: clr
  Register #(.width(32)) register_28 (
    .D(DataIn), .en(decoder_1_out27), .Q(register_28_q), .clk(decoder_1_out27));  // open: clr
  Register #(.width(32)) register_29 (
    .D(DataIn), .en(decoder_1_out28), .Q(register_29_q), .clk(decoder_1_out28));  // open: clr
  Register #(.width(32)) register_30 (
    .D(DataIn), .en(decoder_1_out29), .Q(register_30_q), .clk(decoder_1_out29));  // open: clr
  Register #(.width(32)) register_31 (
    .D(DataIn), .en(decoder_1_out30), .Q(register_31_q), .clk(decoder_1_out30));  // open: clr
  Register #(.width(32)) register_32 (
    .D(DataIn), .en(decoder_1_out31), .Q(register_32_q), .clk(decoder_1_out31));  // open: clr
  Multiplexer #(.select(5), .width(32), .enable("false")) multiplexer_1 (
    .in0(register_1_q), .in1(register_2_q), .in2(register_3_q), .in3(register_4_q), .in4(register_5_q),
    .in5(register_6_q), .in6(register_7_q), .in7(register_8_q), .in8(register_9_q), .in9(register_10_q),
    .in10(register_11_q), .in11(register_12_q), .in12(register_13_q), .in13(register_14_q),
    .in14(register_15_q), .in15(register_16_q), .in16(register_17_q), .in17(register_18_q),
    .in18(register_19_q), .in19(register_20_q), .in20(register_21_q), .in21(register_22_q),
    .in22(register_23_q), .in23(register_24_q), .in24(register_25_q), .in25(register_26_q),
    .in26(register_27_q), .in27(register_28_q), .in28(register_29_q), .in29(register_30_q),
    .in30(register_31_q), .in31(register_32_q), .out(A), .sel(RS));
  Multiplexer #(.select(5), .width(32), .enable("false")) multiplexer_2 (
    .in0(register_1_q), .in1(register_2_q), .in2(register_3_q), .in3(register_4_q), .in4(register_5_q),
    .in5(register_6_q), .in6(register_7_q), .in7(register_8_q), .in8(register_9_q), .in9(register_10_q),
    .in10(register_11_q), .in11(register_12_q), .in12(register_13_q), .in13(register_14_q),
    .in14(register_15_q), .in15(register_16_q), .in16(register_17_q), .in17(register_18_q),
    .in18(register_19_q), .in19(register_20_q), .in20(register_21_q), .in21(register_22_q),
    .in22(register_23_q), .in23(register_24_q), .in24(register_25_q), .in25(register_26_q),
    .in26(register_27_q), .in27(register_28_q), .in28(register_29_q), .in29(register_30_q),
    .in30(register_31_q), .in31(register_32_q), .out(B), .sel(RT));
endmodule

module Mem_Inst (
  input  [31:0] Endereco,
  output [31:0] out_2
);

  ROM #(.addrWidth(16), .dataWidth(32)) rom_1 (.addr(Endereco[15:0]), .data(out_2));  // open: sel

  // Notes on the sheet:
  //   contents of rom_1 (hex, n*v repeats v):
  //   24100000 2411000a 24120003 3c011001 34340000 211a82a 12a00007 210a820 2b5a820 2b4a820 aeb20000
  //   2509020 22100001 1000fff7 8e920000
endmodule

module ULA_32_Bits (
  input  [3:0] Control,
  input  [31:0] A,
  input  [31:0] B,
  output [31:0] Resultado,
  output Zero
);

  wire [31:0] adder_1_out, and_1_out, multiplexer_1_out, multiplexer_2_out, not_1_out, not_2_out, or_1_out,
       xnor_1_out;

  Multiplexer #(.width(32), .enable("false")) multiplexer_1 (
    .in0(A), .in1(not_1_out), .out(multiplexer_1_out), .sel(Control[3]));
  assign not_1_out = ~A;  // NOT_Gate not_1, 32 bits wide
  Multiplexer #(.width(32), .enable("false")) multiplexer_2 (
    .in0(B), .in1(not_2_out), .out(multiplexer_2_out), .sel(Control[2]));
  assign not_2_out = ~B;  // NOT_Gate not_2, 32 bits wide
  assign and_1_out = multiplexer_1_out & multiplexer_2_out;  // AND_Gate and_1, 32 bits wide
  assign or_1_out = multiplexer_1_out | multiplexer_2_out;  // OR_Gate or_1, 32 bits wide
  Adder #(.width(32)) adder_1 (
    .a(multiplexer_1_out), .b(multiplexer_2_out), .out(adder_1_out), .cin(Control[2]));  // open: cout
  Multiplexer #(.select(2), .width(32), .enable("false")) multiplexer_3 (
    .in0(and_1_out), .in1(or_1_out), .in2(adder_1_out), .in3({{31{1'b0}}, adder_1_out[31]}), .out(Resultado),
    .sel(Control[1:0]));
  and and_2 (Zero, xnor_1_out[31], xnor_1_out[30], xnor_1_out[29], xnor_1_out[28], xnor_1_out[27], xnor_1_out[26], xnor_1_out[25], xnor_1_out[24], xnor_1_out[23], xnor_1_out[22], xnor_1_out[21], xnor_1_out[20], xnor_1_out[19], xnor_1_out[18], xnor_1_out[17], xnor_1_out[16], xnor_1_out[15], xnor_1_out[14], xnor_1_out[13], xnor_1_out[12], xnor_1_out[11], xnor_1_out[10], xnor_1_out[9], xnor_1_out[8], xnor_1_out[7], xnor_1_out[6], xnor_1_out[5], xnor_1_out[4], xnor_1_out[3], xnor_1_out[2], xnor_1_out[1], xnor_1_out[0]);
  assign xnor_1_out = ~(B ^ A);  // XNOR_Gate xnor_1, 32 bits wide
endmodule

module Mem_Data (
  input  [31:0] Endereco,
  input  Write,
  input  Read,
  input  [31:0] DataIn,
  output [31:0] DataOut
);

  RAM #(.addrWidth(16), .dataWidth(32), .bus("separate")) ram_1 (
    .addr(Endereco[15:0]), .din(DataIn), .data(DataOut), .str(Write), .ld(Read));  // open: sel, clk, clr
endmodule

module Divisor (
  input  [31:0] Instrucao,
  output [5:0] OP,
  output [4:0] RS,
  output [4:0] RT,
  output [4:0] RD,
  output [4:0] SHAMT,
  output [5:0] FUNCT,
  output [15:0] Imediato
);


  assign FUNCT = Instrucao[5:0];
  assign Imediato = Instrucao[15:0];
  assign OP = Instrucao[31:26];
  assign RD = {Instrucao[11], Instrucao[12], Instrucao[13], Instrucao[14], Instrucao[15]};
  assign RS = Instrucao[25:21];
  assign RT = Instrucao[20:16];
  assign SHAMT = Instrucao[10:6];
endmodule

module Extensor_de_sinal (
  input  [15:0] Sinal_16,
  input  [31:0] Sinal_32
);


  assign Sinal_32 = {{17{Sinal_16[15]}}, Sinal_16[14:0]};
endmodule

module UC (
  input  [5:0] OP,
  output RegDst,
  output ALUSrc,
  output MemtoReg,
  output RegWrite,
  output MemRead,
  output MemWrite,
  output Branch,
  output [1:0] ALUOP
);

  wire Reg_imed_2_out, Reg_imed_3_out, Reg_imed_4_out, Reg_imed_out;

  and Tipo_R (ALUOP[1], ~OP[5], ~OP[4], ~OP[3], ~OP[2], ~OP[1], ~OP[0]);  // AND_Gate
  // Probe on OP
  and lw (MemRead, OP[5], ~OP[4], ~OP[3], ~OP[2], OP[1], OP[0]);  // AND_Gate
  and sw (MemWrite, OP[5], ~OP[4], OP[3], ~OP[2], OP[1], OP[0]);  // AND_Gate
  and beq (ALUOP[0], ~OP[5], ~OP[4], ~OP[3], OP[2], ~OP[1], ~OP[0]);  // AND_Gate
  and Reg_imed (Reg_imed_out, ~OP[5], ~OP[4], OP[3], ~OP[2], ~OP[1], ~OP[0]);  // AND_Gate
  and Reg_imed_2 (Reg_imed_2_out, ~OP[5], ~OP[4], OP[3], ~OP[2], ~OP[1], OP[0]);  // AND_Gate
  and Reg_imed_3 (Reg_imed_3_out, ~OP[5], ~OP[4], OP[3], OP[2], OP[1], OP[0]);  // AND_Gate
  and Reg_imed_4 (Reg_imed_4_out, ~OP[5], ~OP[4], OP[3], ~OP[2], ~OP[1], ~OP[0]);  // AND_Gate
  or or_1 (ALUSrc, Reg_imed_4_out, MemRead, Reg_imed_2_out, Reg_imed_out, MemWrite);
  or or_2 (RegWrite, Reg_imed_4_out, ALUOP[1], Reg_imed_2_out, Reg_imed_out, MemRead, Reg_imed_3_out);

  assign Branch = ALUOP[0];
  assign MemtoReg = MemRead;
  assign RegDst = ALUOP[1];
endmodule

module UC_ULA (
  input  [5:0] Funct,
  input  [1:0] ALUOP,
  output [3:0] Alucontrol
);

  wire and_1_out, or_1_out;

  and and_1 (and_1_out, ALUOP[1], Funct[1]);
  or or_1 (or_1_out, Funct[3], Funct[0]);
  or or_2 (Alucontrol[2], ALUOP[0], and_1_out);
  or or_3 (Alucontrol[1], ~ALUOP[1], ~Funct[2]);  // OR_Gate
  and and_2 (Alucontrol[0], or_1_out, ALUOP[1]);
  // Probe on Funct
  // Probe on {1'b0, Alucontrol[2:0]}

  assign Alucontrol[3] = 1'b0;
endmodule

module teste (
);

  wire [31:0] xnor_1_out;

  assign xnor_1_out = ~(32'hc ^ 32'hd);  // XNOR_Gate xnor_1, 32 bits wide
  // Probe on xnor_1_out
  // AND_Gate and_1 is placed but not wired
endmodule
